# Fritzing sketch TidePoolInitial (saved by Fritzing 0.9.3b)
breadboards: 1

parts:
  Part2 = Arduino Uno (Rev3) - ICSP
  LED1 = RGB LED (com. cathode, rgb) [package="5 mm [THT]"]
  R1 = Resistor [tolerance=±5% resistance=220 package=THT]
  R2 = Resistor [tolerance=±5% resistance=220 package=THT]
  R3 = Resistor [tolerance=±5% resistance=220 package=THT]
  U3 = RELAY [package=relay-t9a-2]
  U4 = RELAY [package=relay-t9a-2]
  S1 = Pushbutton [package=THT]
  S2 = Pushbutton [package=THT]

nets:
  N1: Part2.5V, S1.leg0, S2.leg0
  N2: Part2.GND, LED1.common_cathode, R1.Pin_1, R2.Pin_1, R3.Pin_1, U3.COIL2, U4.COIL2
  N3: Part2.D8, R3.Pin_0
  N4: Part2.D10_PWM/SS, LED1.green_anode
  N5: Part2.D11_PWM/MOSI, LED1.blue_anode
  N6: Part2.D12/MISO, U3.COIL1
  N7: Part2.D13/SCK, U4.COIL1
  N8: Part2.D2, R2.Pin_0, S2.leg1
  N9: Part2.D3_PWM, R1.Pin_0, S1.leg1
  pump2: U3.MAIN
  GND: U3.NC, U4.NC
  120V: U3.NO, U4.NO
  pump1: U4.MAIN

notes:
  pump1
  pump2
  high sensor
  low sensor
