# Fritzing sketch TidePoolProposed (saved by Fritzing 0.9.3b)

parts:
  LED1 = RGB LED (com. cathode, rgb) [package="5 mm [THT]"]
  U4 = RELAY [package=relay-t9a-2]
  U5 = SPM0204UD5 [package=spm0204ud5]
  U3 = RELAY [package=relay-t9a-2]
  Part2 = Arduino Uno (Rev3) - ICSP
  R1 = Resistor [tolerance=±5% resistance=220 package=THT]
  High_Tide_Sensor = SPST Switch [package=switch-spdt_kit]
  Low_Tide_Sensor = SPST Switch [package=switch-spdt_kit]
  R2 = Resistor [tolerance=±5% resistance=220 package=THT]
  R3 = Resistor [tolerance=±5% resistance=220 package=THT]
  Adafruit_HUZZAH_ESP8266_Breakout1 = Adafruit HUZZAH ESP8266 Breakout [part_number=2471]
  Bi-directional_logic_level_converter = Logic Level Converter

nets (from the schematic view):
  GND: LED1.common_cathode, U4.COIL2, U5.GND, U3.COIL2, Part2.GND, R1.Pin_1, R3.Pin_1, Adafruit_HUZZAH_ESP8266_Breakout1.GND, Bi-directional_logic_level_converter.GND
  N1: LED1.green_anode, Part2.D9_PWM
  N2: LED1.blue_anode, Part2.D10_PWM/SS
  N3: U4.COIL1, Part2.D12/MISO
  pump1: U4.MAIN
  120V: U4.NO, U3.NO
  N4: U5.OUT, Part2.D7
  N5: U5.GND#, Part2.D6_PWM
  N6: U5.VS, Part2.5V, Part2.D8, High_Tide_Sensor.O, Low_Tide_Sensor.O, R3.Pin_0, Bi-directional_logic_level_converter.HV
  N7: U3.COIL1, Part2.D11_PWM/MOSI
  pump2: U3.MAIN
  N8: Part2.D2, Low_Tide_Sensor.P
  N9: Part2.D3_PWM, High_Tide_Sensor.P
  N10: Part2.D4, Bi-directional_logic_level_converter.TX_HV
  N11: Part2.D5_PWM, Bi-directional_logic_level_converter.TX2_HV
  N12: Part2.3V3, Adafruit_HUZZAH_ESP8266_Breakout1.V+, Bi-directional_logic_level_converter.LV
  N13: R1.Pin_0, High_Tide_Sensor.S
  N14: Low_Tide_Sensor.S, R2.Pin_0
  N15: Adafruit_HUZZAH_ESP8266_Breakout1.#13, Bi-directional_logic_level_converter.TX_LV
  N16: Adafruit_HUZZAH_ESP8266_Breakout1.#12, Bi-directional_logic_level_converter.TX2_LV

notes:
  pump1
  pump2
  ultrasonic sensor
  reference sensor
